# Fritzing sketch Fritzing Canco (saved by Fritzing 0.9.2b)
breadboards: 1

parts:
  Parte1 = Arduino Uno (Rev3)
  D1 = Rectifier Diode [part_number=1N4001 package="300 mil [THT]"]
  LED2 = LEDs [package=led10mm]
  Q1 = TRANSISTOR_NPN [package=to-92]
  BT1 = Bluetooth HC-06u [package=THT]
  M1 = DC Motor
  R1 = Resistor [tolerance=±5% resistance=220 package="2512 [SMD]"]
  VCC1 = Battery block 9V

nets:
  N1: Parte1.D10_PWM/SS, BT1.TXD
  N2: Parte1.D11_PWM/MOSI, BT1.RXD
  N3: Parte1.D13/SCK, LED2.C
  GND: Parte1.GND, Q1.E, BT1.GND, R1.Pin_0, VCC1.-
  N4: Parte1.D3_PWM, Q1.B
  5V: Parte1.5V, BT1.VCC
  N5: Parte1.VIN, VCC1.+
  N6: D1.cathode, Q1.C, M1.pin_2
  N7: D1.anode, M1.pin_1
  N8: LED2.A, R1.Pin_1

custom parts:
  Bluetooth HC-06u: Bluetooth HC-06 - face up, pins down 16.5mm x 37.5mm PCB
